// Logisim project lab1.5.circ as structural Verilog: 2 circuits, main circuit 4-1MUX
module _4_1MUX (
  input  D0,
  input  D1,
  input  D2,
  input  D3,
  input  S0,
  input  S1,
  output Y
);

  wire and_1_out, and_2_out, and_3_out, and_4_out, and_5_out, and_6_out, and_7_out, and_8_out, not_1_out,
       not_2_out, or_1_out, or_2_out;

  not not_1 (not_1_out, S0);
  and and_1 (and_1_out, not_1_out, not_2_out);
  and and_2 (and_2_out, not_1_out, S1);
  and and_3 (and_3_out, S0, not_2_out);
  not not_2 (not_2_out, S1);
  and and_4 (and_4_out, S0, S1);
  and and_5 (and_5_out, D0, and_1_out);
  and and_6 (and_6_out, D2, and_2_out);
  and and_7 (and_7_out, D1, and_3_out);
  and and_8 (and_8_out, D3, and_4_out);
  or or_1 (or_1_out, and_5_out, and_6_out);
  or or_2 (or_2_out, and_7_out, and_8_out);
  or or_3 (Y, or_1_out, or_2_out);

  // Notes on the sheet:
  //   输入引脚
  //   请勿修改引脚名称、电路名称及电路封装外观
  //   提示：使用二选一多路选择器子电路级联实现四选一多路选择器，禁止直接使用多路选择器组件。
  //   输出引脚
endmodule

module _2_1MUX (
  input  D0,
  input  D1,
  input  S,
  output Y
);


  // Notes on the sheet:
  //   输入引脚
  //   请勿修改引脚名称及电路封装外观
  //   提示：使用传输门和晶体管来实现二选一多路选择器，禁止直接使用选择器组件。
  //   输出引脚
endmodule
