// Logisim project lab2.1.circ as structural Verilog: 1 circuit, main circuit main
module main (
  input  G1,
  input  G2A_L,
  input  G2B_L,
  input  A,
  input  B,
  input  C,
  input  in_7,
  input  in_8,
  input  in_9,
  input  in_10,
  input  in_11,
  input  in_12,
  output Y0_L,
  output Y1_L,
  output Y2_L,
  output Y3_L,
  output Y4_L,
  output Y5_L,
  output Y6_L,
  output Y7_L,
  output out_21,
  output out_22,
  output out_23,
  output out_24,
  output out_25,
  output out_26,
  output out_27,
  output out_28
);

  wire and_1_out, not_1_out, not_2_out, not_3_out, not_4_out, not_5_out, not_6_out, not_7_out, not_8_out;

  not not_1 (not_1_out, G2A_L);
  not not_2 (not_2_out, G2B_L);
  and and_1 (and_1_out, G1, not_1_out, not_2_out);
  not not_3 (not_3_out, A);
  not not_4 (not_4_out, B);
  not not_5 (not_5_out, C);
  not not_6 (not_6_out, not_3_out);
  not not_7 (not_7_out, not_4_out);
  not not_8 (not_8_out, not_5_out);
  nand nand_1 (out_21, not_3_out, not_4_out, not_5_out, and_1_out);
  nand nand_2 (out_22, not_4_out, not_5_out, not_6_out, and_1_out);
  nand nand_3 (out_23, not_3_out, not_7_out, not_5_out, and_1_out);
  nand nand_4 (out_24, not_5_out, not_6_out, not_7_out, and_1_out);
  nand nand_5 (out_25, not_3_out, not_4_out, not_8_out, and_1_out);
  nand nand_6 (out_26, not_4_out, not_6_out, not_8_out, and_1_out);
  nand nand_7 (out_27, not_3_out, not_7_out, not_8_out, and_1_out);
  nand nand_8 (out_28, and_1_out, not_7_out, not_8_out, not_6_out);

  assign in_7 = G1;
  assign in_8 = G2A_L;
  assign in_9 = G2B_L;
  assign in_10 = A;
  assign in_11 = B;
  assign in_12 = C;
  assign Y0_L = out_21;
  assign Y1_L = out_22;
  assign Y2_L = out_23;
  assign Y3_L = out_24;
  assign Y4_L = out_25;
  assign Y5_L = out_26;
  assign Y6_L = out_27;
  assign Y7_L = out_28;

  // Notes on the sheet:
  //   输入引脚
  //   请勿修改引脚名称、电路名称及电路封装外观
  //   提示：使用独立逻辑门实现3-8译码器，禁止直接使用译码器组件。
  //   输出引脚
endmodule
