// Logisim project lab2.3.circ as structural Verilog: 2 circuits, main circuit main
module main (
  input  [3:0] X,
  input  [3:0] Y,
  input  Cin,
  output [3:0] F,
  output Cout
);

  wire and_1_out, FA0_cout, FA1_cout, FA2_cout, FA3_cout, fa_1_cout, fa_2_cout, fa_3_cout, fa_4_cout,
       not_1_out, not_2_out, not_3_out, not_4_out;
  wire [3:0] minus_y, multiplexer_1_out;

  Hex_Digit_Display hex_digit_display_1 (.value(X));  // open: dp
  Multiplexer #(.width(4), .enable("false")) multiplexer_1 (.in0(Y), .in1(minus_y), .out(multiplexer_1_out), .sel(Cin));
  not not_1 (not_1_out, Y[0]);
  not not_2 (not_2_out, Y[1]);
  not not_3 (not_3_out, Y[2]);
  not not_4 (not_4_out, Y[3]);
  Hex_Digit_Display hex_digit_display_2 (.value(Y));  // open: dp
  FA FA0 (.A(X[0]), .B(multiplexer_1_out[0]), .Cin(1'b0), .Cout(FA0_cout), .F(F[0]));
  FA fa_1 (.A(not_1_out), .B(1'b1), .Cin(1'b0), .Cout(fa_1_cout), .F(minus_y[0]));
  Hex_Digit_Display hex_digit_display_3 (.value(F));  // open: dp
  FA FA1 (.A(X[1]), .B(multiplexer_1_out[1]), .Cin(FA0_cout), .Cout(FA1_cout), .F(F[1]));
  FA fa_2 (.A(not_2_out), .B(1'b0), .Cin(fa_1_cout), .Cout(fa_2_cout), .F(minus_y[1]));
  FA FA2 (.A(X[2]), .B(multiplexer_1_out[2]), .Cin(FA1_cout), .Cout(FA2_cout), .F(F[2]));
  FA fa_3 (.A(not_3_out), .B(1'b0), .Cin(fa_2_cout), .Cout(fa_3_cout), .F(minus_y[2]));
  FA fa_4 (.A(not_4_out), .B(1'b0), .Cin(fa_3_cout), .Cout(fa_4_cout), .F(minus_y[3]));
  FA FA3 (.A(X[3]), .B(multiplexer_1_out[3]), .Cin(FA2_cout), .Cout(FA3_cout), .F(F[3]));
  and and_1 (and_1_out, Cin, fa_4_cout);
  or or_1 (Cout, FA3_cout, and_1_out);

  // Other names for the same wires on the sheet: SUM[3:0] = F; 操作数x[3:0] = X; 操作数y[3:0] = Y

  // Notes on the sheet:
  //   输入引脚
  //   +
  //   =
  //   请勿修改引脚名称、电路名称及电路封装外观
  //   提示：使用独立逻辑门及全加器FA子电路实现4位二进制数加减法器，禁止直接使用加减法器组件。
  //   输出引脚
endmodule

module FA (
  input  A,
  input  B,
  input  Cin,
  output F,
  output Cout
);

  wire and_1_out, and_2_out, and_3_out, xor_1_out;

  xor xor_1 (xor_1_out, A, B);
  and and_1 (and_1_out, A, B);
  and and_2 (and_2_out, B, Cin);
  and and_3 (and_3_out, A, Cin);
  xor xor_2 (F, xor_1_out, Cin);
  or or_1 (Cout, and_1_out, and_2_out, and_3_out);

  // Notes on the sheet:
  //   全加器
endmodule
