// Logisim project lab2.5.circ as structural Verilog: 5 circuits, main circuit main
module main (
  input  [7:0] DataIn,
  input  [2:0] shamt,
  input  L_R,
  input  A_L,
  output [7:0] DataOut
);

  wire [7:0] multiplexer_1_out, multiplexer_2_out, multiplexer_3_out, multiplexer_4_out, multiplexer_5_out,
       n00_1_out_2, n00_2_out_2, n00_3_out_2, n00_4_out_2, n00_5_out_2, n00_6_out_2, n00_7_out_2,
       n01_1_out_2, n01_2_out_2, n01_3_out_2, n01_4_out_2, n01_5_out_2, n01_6_out_2, n01_7_out_2,
       n10_1_out_2, n10_2_out_2, n10_3_out_2, n10_4_out_2, n10_5_out_2, n10_6_out_2, n10_7_out_2,
       n11_1_out_2, n11_2_out_2, n11_3_out_2, n11_4_out_2, n11_5_out_2, n11_6_out_2, n11_7_out_2;

  _00 u_00_1 (.in_1(DataIn), .out_2(n00_1_out_2));
  _01 u_01_1 (.in_1(DataIn), .out_2(n01_1_out_2));
  _10 u_10_1 (.in_1(DataIn), .out_2(n10_1_out_2));
  _11 u_11_1 (.in_1(DataIn), .out_2(n11_1_out_2));
  Multiplexer #(.select(2), .width(8), .enable("false")) multiplexer_1 (
    .in0(n00_1_out_2), .in1(n01_1_out_2), .in2(n10_1_out_2), .in3(n11_1_out_2), .out(multiplexer_1_out),
    .sel({L_R, A_L}));
  Multiplexer #(.width(8), .enable("false")) multiplexer_2 (
    .in0(DataIn), .in1(multiplexer_1_out), .out(multiplexer_2_out), .sel(shamt[0]));
  _00 u_00_2 (.in_1(multiplexer_2_out), .out_2(n00_2_out_2));
  _01 u_01_2 (.in_1(multiplexer_2_out), .out_2(n01_2_out_2));
  _10 u_10_2 (.in_1(multiplexer_2_out), .out_2(n10_2_out_2));
  _11 u_11_2 (.in_1(multiplexer_2_out), .out_2(n11_2_out_2));
  _00 u_00_3 (.in_1(n00_2_out_2), .out_2(n00_3_out_2));
  _01 u_01_3 (.in_1(n01_2_out_2), .out_2(n01_3_out_2));
  _10 u_10_3 (.in_1(n10_2_out_2), .out_2(n10_3_out_2));
  _11 u_11_3 (.in_1(n11_2_out_2), .out_2(n11_3_out_2));
  Multiplexer #(.select(2), .width(8), .enable("false")) multiplexer_3 (
    .in0(n00_3_out_2), .in1(n01_3_out_2), .in2(n10_3_out_2), .in3(n11_3_out_2), .out(multiplexer_3_out),
    .sel({L_R, A_L}));
  Multiplexer #(.width(8), .enable("false")) multiplexer_4 (
    .in0(multiplexer_2_out), .in1(multiplexer_3_out), .out(multiplexer_4_out), .sel(shamt[1]));
  _00 u_00_4 (.in_1(multiplexer_4_out), .out_2(n00_4_out_2));
  _01 u_01_4 (.in_1(multiplexer_4_out), .out_2(n01_4_out_2));
  _10 u_10_4 (.in_1(multiplexer_4_out), .out_2(n10_4_out_2));
  _11 u_11_4 (.in_1(multiplexer_4_out), .out_2(n11_4_out_2));
  _00 u_00_5 (.in_1(n00_4_out_2), .out_2(n00_5_out_2));
  _00 u_00_6 (.in_1(n00_5_out_2), .out_2(n00_6_out_2));
  _01 u_01_5 (.in_1(n01_4_out_2), .out_2(n01_5_out_2));
  _01 u_01_6 (.in_1(n01_5_out_2), .out_2(n01_6_out_2));
  _10 u_10_5 (.in_1(n10_6_out_2), .out_2(n10_5_out_2));
  _10 u_10_6 (.in_1(n10_4_out_2), .out_2(n10_6_out_2));
  _11 u_11_5 (.in_1(n11_6_out_2), .out_2(n11_5_out_2));
  _11 u_11_6 (.in_1(n11_4_out_2), .out_2(n11_6_out_2));
  _00 u_00_7 (.in_1(n00_6_out_2), .out_2(n00_7_out_2));
  _01 u_01_7 (.in_1(n01_6_out_2), .out_2(n01_7_out_2));
  _10 u_10_7 (.in_1(n10_5_out_2), .out_2(n10_7_out_2));
  _11 u_11_7 (.in_1(n11_5_out_2), .out_2(n11_7_out_2));
  Multiplexer #(.select(2), .width(8), .enable("false")) multiplexer_5 (
    .in0(n00_7_out_2), .in1(n01_7_out_2), .in2(n10_7_out_2), .in3(n11_7_out_2), .out(multiplexer_5_out),
    .sel({L_R, A_L}));
  Multiplexer #(.width(8), .enable("false")) multiplexer_6 (
    .in0(multiplexer_4_out), .in1(multiplexer_5_out), .out(DataOut), .sel(shamt[2]));

  // Other names for the same wires on the sheet: Arth_Logic = A_L; Left_Right = L_R; Din[7:0] = DataIn;
  //   Dout[7:0] = DataOut

  // Notes on the sheet:
  //   L/R,A/L: 00逻辑右移，01算术右移，10逻辑左移，11：循环左移
  //   输入引脚
  //   请勿修改引脚名称、电路名称及电路封装外观
  //   输出引脚
endmodule

module _00 (
  input  [7:0] in_1,
  output [7:0] out_2
);


  assign out_2 = {1'b0, in_1[7:1]};
endmodule

module _01 (
  input  [7:0] in_1,
  output [7:0] out_2
);


  assign out_2 = {{2{in_1[7]}}, in_1[6:1]};
endmodule

module _10 (
  input  [7:0] in_1,
  output [7:0] out_2
);


  assign out_2 = {in_1[6:0], 1'b0};
endmodule

module _11 (
  input  [7:0] in_1,
  output [7:0] out_2
);


  assign out_2 = {in_1[6:0], in_1[7]};
endmodule
