// Logisim project lab3.5.circ as structural Verilog: 2 circuits, main circuit main
module main (
  input  CLK,
  input  LD,
  input  [3:0] HH1,
  input  [3:0] HH0,
  input  [3:0] MM1,
  input  [3:0] MM0,
  input  [3:0] SS1,
  input  [3:0] SS0,
  output out_9,
  output [3:0] HH_H,
  output [3:0] HH_L,
  output [3:0] MM_H,
  output [3:0] MM_L,
  output out_14,
  output [3:0] SS_H,
  output [3:0] SS_L,
  output out_17,
  output LED_R,
  output LED_G,
  output LED_B,
  output INErr
);

  wire and_2_out, and_3_out, and_4_out, and_5_out, and_6_out, and_7_out, and_8_out, and_10_out, and_11_out,
       comparator_1_eq, comparator_1_gt, comparator_2_gt, comparator_3_gt, comparator_4_gt, comparator_5_gt,
       comparator_6_gt, comparator_7_gt, comparator_8_eq, comparator_9_lt, comparator_10_gt, not_1_out,
       or_1_out, or_2_out, or_3_out, or_4_out, or_5_out, temp;
  wire [3:0] cntr4u_4_q0, cntr4u_5_q0, multiplexer_1_out, subtractor_1_out;
  wire [3:3] gray_1_out_2;

  not not_1 (not_1_out, INErr);
  and and_1 (temp, LD, not_1_out);
  Comparator #(.width(4), .mode("unsigned")) comparator_1 (
    .a(HH1), .b(4'b0010), .gt(comparator_1_gt), .eq(comparator_1_eq));  // open: lt
  Comparator #(.width(4), .mode("unsigned")) comparator_2 (.a(HH0), .b(4'b0011), .gt(comparator_2_gt));  // open: eq, lt
  Comparator #(.width(4), .mode("unsigned")) comparator_3 (.a(HH0), .b(4'b1001), .gt(comparator_3_gt));  // open: eq, lt
  Comparator #(.width(4), .mode("unsigned")) comparator_4 (.a(MM1), .b(4'b0101), .gt(comparator_4_gt));  // open: eq, lt
  Comparator #(.width(4), .mode("unsigned")) comparator_5 (.a(MM0), .b(4'b1001), .gt(comparator_5_gt));  // open: eq, lt
  Comparator #(.width(4), .mode("unsigned")) comparator_6 (.a(SS1), .b(4'b0101), .gt(comparator_6_gt));  // open: eq, lt
  Comparator #(.width(4), .mode("unsigned")) comparator_7 (.a(SS0), .b(4'b1001), .gt(comparator_7_gt));  // open: eq, lt
  Hex_Digit_Display hex_digit_display_1 (.value(HH_H));  // open: dp
  CNTR4U cntr4u_1 (
    .CLK(CLK), .LD(temp), .CLR(or_4_out), .Q0(HH_L[0]), .Q1(HH_L[1]), .D0(HH0[0]), .D1(HH0[1]), .D2(HH0[2]),
    .Q2(HH_L[2]), .Q3(HH_L[3]), .D3(HH0[3]), .ENP(and_11_out), .ENT(and_11_out));  // open: RCO
  CNTR4U cntr4u_2 (
    .CLK(CLK), .LD(temp), .CLR(and_4_out), .Q0(MM_L[0]), .Q1(MM_L[1]), .D0(MM0[0]), .D1(MM0[1]), .D2(MM0[2]),
    .Q2(MM_L[2]), .Q3(MM_L[3]), .D3(MM0[3]), .ENP(and_8_out), .ENT(and_8_out));  // open: RCO
  CNTR4U cntr4u_3 (
    .CLK(CLK), .LD(temp), .CLR(and_5_out), .Q0(SS_L[0]), .Q1(SS_L[1]), .D0(SS0[0]), .D1(SS0[1]), .D2(SS0[2]),
    .Q2(SS_L[2]), .Q3(SS_L[3]), .D3(SS0[3]), .ENP(1'b1), .ENT(1'b1));  // open: RCO
  and and_2 (and_2_out, comparator_1_eq, comparator_2_gt);
  CNTR4U cntr4u_4 (
    .CLK(CLK), .LD(out_14), .CLR(out_17), .Q0(cntr4u_4_q0[0]), .Q1(cntr4u_4_q0[1]), .D0(1'b1), .D1(1'b0),
    .D2(1'b0), .Q2(cntr4u_4_q0[2]), .Q3(cntr4u_4_q0[3]), .D3(1'b0), .ENP(out_9), .ENT(out_9));  // open: RCO
  Hex_Digit_Display hex_digit_display_2 (.value(MM_H));  // open: dp
  Hex_Digit_Display hex_digit_display_3 (.value(HH_L), .dp(1'b1));
  and and_3 (and_3_out, HH_L[0], HH_L[3], and_11_out);
  and and_4 (and_4_out, and_8_out, MM_L[0], MM_L[3]);
  and and_5 (and_5_out, SS_L[0], SS_L[3]);
  and and_6 (and_6_out, and_5_out, and_8_out);
  or or_1 (or_1_out, comparator_1_gt, and_2_out, comparator_3_gt);
  or or_2 (or_2_out, comparator_4_gt, comparator_5_gt);
  or or_3 (or_3_out, comparator_6_gt, comparator_7_gt);
  Multiplexer #(.width(4), .enable("false")) multiplexer_1 (
    .in0(4'b0000), .in1(cntr4u_4_q0), .out(multiplexer_1_out), .sel(out_9));
  Hex_Digit_Display hex_digit_display_4 (.value(MM_L), .dp(1'b1));
  Hex_Digit_Display hex_digit_display_5 (.value(SS_H));  // open: dp
  or or_4 (or_4_out, and_3_out, and_10_out);
  and and_7 (and_7_out, MM_L[0], MM_L[3], MM_H[0], MM_H[2]);
  and and_8 (and_8_out, and_5_out, SS_H[0], SS_H[2]);
  gray gray_1 (.in_1(multiplexer_1_out), .out_2({gray_1_out_2[3], LED_B, LED_G, LED_R}));
  Comparator #(.width(4), .mode("unsigned")) comparator_8 (
    .a(cntr4u_4_q0), .b(4'b0000), .eq(comparator_8_eq));  // open: gt, lt
  Comparator #(.width(4), .mode("unsigned")) comparator_9 (
    .a(cntr4u_4_q0), .b(4'b1010), .lt(comparator_9_lt));  // open: gt, eq
  Hex_Digit_Display hex_digit_display_6 (.value(SS_L), .dp(1'b1));
  or or_5 (or_5_out, or_1_out, or_2_out, or_3_out);
  and and_9 (INErr, or_5_out, LD);
  not not_2 (out_9, comparator_8_eq);
  not not_3 (out_17, comparator_9_lt);
  CNTR4U cntr4u_5 (
    .CLK(CLK), .LD(temp), .CLR(and_10_out), .Q0(cntr4u_5_q0[0]), .Q1(cntr4u_5_q0[1]), .D0(HH1[0]),
    .D1(HH1[1]), .D2(HH1[2]), .Q2(cntr4u_5_q0[2]), .Q3(cntr4u_5_q0[3]), .D3(HH1[3]), .ENP(and_3_out),
    .ENT(and_3_out));  // open: RCO
  and and_10 (and_10_out, and_11_out, HH_L[0], HH_L[1], cntr4u_5_q0[1]);
  CNTR4U cntr4u_6 (
    .CLK(CLK), .LD(temp), .CLR(and_11_out), .Q0(MM_H[0]), .Q1(MM_H[1]), .D0(MM1[0]), .D1(MM1[1]),
    .D2(MM1[2]), .Q2(MM_H[2]), .Q3(MM_H[3]), .D3(MM1[3]), .ENP(and_4_out), .ENT(and_4_out));  // open: RCO
  and and_11 (and_11_out, and_4_out, and_8_out, MM_H[2], MM_H[0]);
  CNTR4U cntr4u_7 (
    .CLK(CLK), .LD(temp), .CLR(and_8_out), .Q0(SS_H[0]), .Q1(SS_H[1]), .D0(SS1[0]), .D1(SS1[1]), .D2(SS1[2]),
    .Q2(SS_H[2]), .Q3(SS_H[3]), .D3(SS1[3]), .ENP(and_5_out), .ENT(and_5_out));  // open: RCO
  // RGBLed RGBLED: pin names not known; wires that end beside it: LED_R, LED_G, LED_B
  Multiplexer #(.width(4), .enable("false")) multiplexer_2 (
    .in0(cntr4u_5_q0), .in1(subtractor_1_out), .out(HH_H), .sel(comparator_10_gt));
  Comparator #(.width(4), .mode("unsigned")) comparator_10 (
    .a(cntr4u_5_q0), .b(4'b0010), .gt(comparator_10_gt));  // open: eq, lt
  Subtractor #(.width(4)) subtractor_1 (.a(cntr4u_5_q0), .b(4'b0011), .out(subtractor_1_out));  // open: bin, bout
  and and_12 (out_14, and_7_out, and_6_out);

  // Other names for the same wires on the sheet: H0[3:0] = HH_L; H1[3:0] = HH_H; LED_EN = out_14; M0[3:0] = MM_L;
  //   M1[3:0] = MM_H; S0[3:0] = SS_L; S1[3:0] = SS_H; START = out_9; STOP = out_17

  // Notes on the sheet:
  //   设置初始时间BCD码
  //   输入信号
  //   请勿修改引脚名称、电路名称及电路封装外观
  //   数字时钟
  //   提示：使用4位二进制加法计数器子电路、比较器和独立逻辑门组件实现数字时钟。
  //   在载入有效时，检测设置数据错误
  //   生成三色LED显示信号，持续10个时钟周期
endmodule

module gray (
  input  [3:0] in_1,
  output [3:0] out_2
);

  xor xor_1 (out_2[0], in_1[0], in_1[1]);
  xor xor_2 (out_2[1], in_1[1], in_1[2]);
  xor xor_3 (out_2[2], in_1[2], 1'b0);

  assign out_2[3] = 1'b0;
endmodule
