// Logisim project lab4.3.circ as structural Verilog: 2 circuits, main circuit Adder32
// 加法器
module Adder32 (
  input  Cin,
  input  [31:0] X,
  input  [31:0] Y,
  output CF,
  output Cout,
  output OF,
  output SF,
  output [31:0] S,
  output ZF
);

  wire and_2_out, and_3_out, main_2_c16, zf_1_out_2, zf_2_out_2;

  and and_1 (ZF, zf_1_out_2, zf_2_out_2);
  zf zf_1 (.in_1(S[31:16]), .out_2(zf_1_out_2));
  zf zf_2 (.in_1(S[15:0]), .out_2(zf_2_out_2));
  lab4_2_main main_1 (.X(X[31:16]), .Y(Y[31:16]), .C0(main_2_c16), .S(S[31:16]), .C16(Cout));  // open: Pg, Gg
  lab4_2_main main_2 (.X(X[15:0]), .Y(Y[15:0]), .C0(Cin), .S(S[15:0]), .C16(main_2_c16));  // open: Pg, Gg
  xor xor_1 (CF, Cin, Cout);
  and and_2 (and_2_out, Y[31], X[31], ~S[31]);  // AND_Gate
  or or_1 (OF, and_2_out, and_3_out);
  and and_3 (and_3_out, ~Y[31], ~X[31], S[31]);  // AND_Gate
  // Probe on X
  // Probe on Y
  // Probe on S

  assign SF = S[31];

  // Notes on the sheet:
  //   Y: pull=down
  //   X: pull=down
  //   Cin: pull=down
  //   输入引脚区
  //   输出引脚区
  //   请勿修改引脚名称、电路名称及电路封装外观
  //   提示：使用16位并行加法器子电路实现32位快速加法器
  //   功能说明:32位Adder  S=X+Y，Cout为最高位进位位，Cin为进位输入， S为和，溢出OF、进位CF、零ZF、符号SF。
  //   +
  //   =
  //   无符号加法
endmodule

module zf (
  input  [15:0] in_1,
  output out_2
);

  nor nor_1 (out_2, in_1[0], in_1[1], in_1[2], in_1[3], in_1[4], in_1[5], in_1[6], in_1[7], in_1[8], in_1[9], in_1[10], in_1[11], in_1[12], in_1[13], in_1[14], in_1[15]);
endmodule
