// Logisim project 思考题1.circ as structural Verilog: 12 circuits, main circuit 32*32
module main (
  input  CLK,
  input  [3:0] X,
  input  [3:0] Y,
  input  Reset,
  output [7:0] Prod
);

  wire LOAD, not_1_out, STOP;
  wire [3:0] \_4位同步计数器_q0 , adder4b_1_cout, adder4b_1_f, multiplexer_1_out, multiplexer_2_out,
       \桶形移位器_dataout ;
  wire [3:3] \桶形移位器_dataout_2 ;

  Multiplexer #(.width(4), .enable("false")) multiplexer_1 (
    .in0(4'b0000), .in1(X), .out(multiplexer_1_out), .sel(Prod[0]));
  Hex_Digit_Display hex_digit_display_1 (.value(X));  // open: dp
  not not_1 (not_1_out, STOP);
  ADDER4b adder4b_1 (.X(Prod[7:4]), .Y(multiplexer_1_out), .F(adder4b_1_f), .Cout(adder4b_1_cout[3]), .Cin(1'b0));
  Hex_Digit_Display hex_digit_display_2 (.value(Y));  // open: dp
  Register #(.width(4), .Select("low")) register_1 (
    .D(adder4b_1_cout), .en(not_1_out), .Q(Prod[7:4]), .clk(CLK), .clr(Reset));
  Hex_Digit_Display hex_digit_display_3 (.value(Prod[7:4]));  // open: dp
  // Probe on Prod[7:4]
  BarrelSFT8b \u_桶形移位器  (
    .DataIn({adder4b_1_f, Prod[3:0]}), .shamt(3'b001), .L_R(1'b0), .A_L(1'b0),
    .DataOut({\桶形移位器_dataout_2 [3], adder4b_1_cout[2:0], \桶形移位器_dataout }));
  Hex_Digit_Display hex_digit_display_4 (.value(Prod[3:0]));  // open: dp
  // Probe on Prod[3:0]
  Register #(.width(4), .Select("low")) Y_2 (
    .D(multiplexer_2_out), .en(not_1_out), .Q(Prod[3:0]), .clk(CLK), .clr(Reset));
  Multiplexer #(.width(4), .enable("false")) multiplexer_2 (
    .in0(\桶形移位器_dataout ), .in1(Y), .out(multiplexer_2_out), .sel(LOAD));
  // Probe on X
  // Probe on Y
  // Probe on Prod
  CNTR4U \_4位同步计数器  (
    .CLK(CLK), .LD(1'b0), .CLR(Reset), .Q0(\_4位同步计数器_q0 [0]), .Q1(\_4位同步计数器_q0 [1]), .Q2(\_4位同步计数器_q0 [2]),
    .Q3(\_4位同步计数器_q0 [3]), .ENP(not_1_out), .ENT(not_1_out));  // open: D0, D1, D2, D3, RCO
  Comparator #(.width(4)) comparator_1 (.a(\_4位同步计数器_q0 ), .b(4'b0000), .eq(LOAD));  // open: gt, lt
  Comparator #(.width(4)) comparator_2 (.a(\_4位同步计数器_q0 ), .b(4'b0101), .eq(STOP));  // open: gt, lt

  // Other names for the same wires on the sheet: RST = Reset; Z[7:0] = Prod

  // Notes on the sheet:
  //   X
  //   输入引脚
  //   P
  //   =
  //   请勿修改引脚名称、电路名称及电路封装外观
  //   提示: 采用无符号数一位乘法实现4位二进制乘法器，禁止直接使用乘法器组件
  //   ×
  //   =
  //   输出引脚
endmodule

module CNTR4U (
  input  CLK,
  input  LD,
  input  CLR,
  input  D0,
  input  D1,
  input  D2,
  input  D3,
  input  ENP,
  input  ENT,
  output Q0,
  output Q1,
  output Q2,
  output Q3,
  output RCO
);

  wire and_1_out, and_2_out, and_3_out, and_4_out, and_5_out, and_6_out, and_7_out, and_8_out, and_9_out,
       and_10_out, and_11_out, and_12_out, and_13_out, and_14_out, and_15_out, and_16_out, buffer_1_out,
       d_ff_1_qn, d_ff_2_qn, d_ff_3_qn, d_ff_4_qn, not_1_out, not_2_out, or_1_out, or_2_out, or_3_out,
       or_4_out, xor_1_out, xor_2_out, xor_3_out, xor_4_out;

  buf buffer_1 (buffer_1_out, CLR);
  not not_1 (not_1_out, CLK);
  and and_1 (and_1_out, ~d_ff_1_qn, and_6_out);  // AND_Gate
  and and_2 (and_2_out, ~d_ff_1_qn, ~d_ff_2_qn);  // AND_Gate
  and and_3 (and_3_out, and_2_out, and_6_out);
  and and_4 (and_4_out, ~d_ff_1_qn, ~d_ff_2_qn, ~d_ff_3_qn);  // AND_Gate
  and and_5 (and_5_out, and_4_out, and_6_out);
  and and_6 (and_6_out, ENP, ENT);
  not not_2 (not_2_out, ENT);
  and and_7 (and_7_out, LD, ~buffer_1_out);  // AND_Gate
  and and_8 (and_8_out, ~and_7_out, ~buffer_1_out);  // AND_Gate
  xor xor_1 (xor_1_out, and_6_out, ~d_ff_1_qn);  // XOR_Gate
  xor xor_2 (xor_2_out, and_1_out, ~d_ff_2_qn);  // XOR_Gate
  xor xor_3 (xor_3_out, and_3_out, ~d_ff_3_qn);  // XOR_Gate
  xor xor_4 (xor_4_out, and_5_out, ~d_ff_4_qn);  // XOR_Gate
  and and_9 (and_9_out, and_7_out, D0);
  and and_10 (and_10_out, and_8_out, xor_1_out);
  and and_11 (and_11_out, and_7_out, D1);
  and and_12 (and_12_out, and_8_out, xor_2_out);
  and and_13 (and_13_out, and_7_out, D2);
  and and_14 (and_14_out, and_8_out, xor_3_out);
  and and_15 (and_15_out, and_7_out, D3);
  and and_16 (and_16_out, and_8_out, xor_4_out);
  and and_17 (RCO, ~d_ff_4_qn, ~d_ff_1_qn, ~d_ff_2_qn, ~d_ff_3_qn, ~not_2_out);  // AND_Gate
  or or_1 (or_1_out, and_9_out, and_10_out);
  or or_2 (or_2_out, and_11_out, and_12_out);
  or or_3 (or_3_out, and_13_out, and_14_out);
  or or_4 (or_4_out, and_15_out, and_16_out);
  D_Flip_Flop #(.trigger("falling")) d_ff_1 (
    .clk(not_1_out), .D(or_1_out), .Q(Q0), .Qn(d_ff_1_qn));  // open: preset, reset
  D_Flip_Flop #(.trigger("falling")) d_ff_2 (
    .clk(not_1_out), .D(or_2_out), .Q(Q1), .Qn(d_ff_2_qn));  // open: preset, reset
  D_Flip_Flop #(.trigger("falling")) d_ff_3 (
    .clk(not_1_out), .D(or_3_out), .Q(Q2), .Qn(d_ff_3_qn));  // open: preset, reset
  D_Flip_Flop #(.trigger("falling")) d_ff_4 (
    .clk(not_1_out), .D(or_4_out), .Q(Q3), .Qn(d_ff_4_qn));  // open: preset, reset

  // Notes on the sheet:
  //   输入引脚
  //   请勿修改引脚名称、电路名称及电路封装外观
  //   提示：使用独立逻辑门实现4位二进制同步计数器，禁止直接使用计数器组件。
  //   输出引脚
endmodule

module ADDER4b (
  input  [3:0] X,
  input  [3:0] Y,
  input  Cin,
  output [3:0] F,
  output Cout
);

  wire fa_1_cout, fa_2_cout, fa_3_cout;
  wire [3:0] bit_extender_1_out, xor_1_out;

  assign bit_extender_1_out = {{3{Cin}}, Cin};  // Bit_Extender bit_extender_1
  Hex_Digit_Display hex_digit_display_1 (.value(X), .dp(1'b0));
  assign xor_1_out = bit_extender_1_out ^ Y;  // XOR_Gate xor_1, 4 bits wide
  Hex_Digit_Display hex_digit_display_2 (.value(xor_1_out), .dp(1'b0));
  FA fa_1 (.A(X[0]), .B(xor_1_out[0]), .Cin(Cin), .F(F[0]), .Cout(fa_1_cout));
  Hex_Digit_Display hex_digit_display_3 (.value(F), .dp(1'b0));
  FA fa_2 (.A(X[1]), .B(xor_1_out[1]), .Cin(fa_1_cout), .F(F[1]), .Cout(fa_2_cout));
  FA fa_3 (.A(X[2]), .B(xor_1_out[2]), .Cin(fa_2_cout), .F(F[2]), .Cout(fa_3_cout));
  FA fa_4 (.A(X[3]), .B(xor_1_out[3]), .Cin(fa_3_cout), .F(F[3]), .Cout(Cout));

  // Other names for the same wires on the sheet: SUM[3:0] = F; 操作数x[3:0] = X; 操作数y[3:0] = Y

  // Notes on the sheet:
  //   输入引脚
  //   +
  //   =
  //   请勿修改引脚名称、电路名称及电路封装外观
  //   提示：使用独立逻辑门及全加器FA子电路实现4位二进制数加减法器，禁止直接使用加减法器组件。
  //   输出引脚
endmodule

module FA (
  input  A,
  input  B,
  input  Cin,
  output F,
  output Cout
);

  wire and_1_out, and_2_out, and_3_out;

  xor xor_1 (F, A, B, Cin);
  and and_1 (and_1_out, A, B);
  and and_2 (and_2_out, B, Cin);
  and and_3 (and_3_out, A, Cin);
  or or_1 (Cout, and_1_out, and_2_out, and_3_out);

  // Notes on the sheet:
  //   全加器
endmodule

module BarrelSFT8b (
  input  [7:0] DataIn,
  input  [2:0] shamt,
  input  L_R,
  input  A_L,
  output [7:0] DataOut
);

  wire [7:0] multiplexer_1_out, multiplexer_2_out, multiplexer_3_out, multiplexer_4_out, multiplexer_5_out,
       n00_1_out_2, n00_2_out_2, n00_3_out_2, n00_4_out_2, n00_5_out_2, n00_6_out_2, n00_7_out_2,
       n01_1_out_2, n01_2_out_2, n01_3_out_2, n01_4_out_2, n01_5_out_2, n01_6_out_2, n01_7_out_2,
       n10_1_out_2, n10_2_out_2, n10_3_out_2, n10_4_out_2, n10_5_out_2, n10_6_out_2, n10_7_out_2,
       n11_1_out_2, n11_2_out_2, n11_3_out_2, n11_4_out_2, n11_5_out_2, n11_6_out_2, n11_7_out_2;

  _00 u_00_1 (.in_1(DataIn), .out_2(n00_1_out_2));
  _01 u_01_1 (.in_1(DataIn), .out_2(n01_1_out_2));
  _10 u_10_1 (.in_1(DataIn), .out_2(n10_1_out_2));
  _11 u_11_1 (.in_1(DataIn), .out_2(n11_1_out_2));
  Multiplexer #(.select(2), .width(8), .enable("false")) multiplexer_1 (
    .in0(n00_1_out_2), .in1(n01_1_out_2), .in2(n10_1_out_2), .in3(n11_1_out_2), .out(multiplexer_1_out),
    .sel({L_R, A_L}));
  Multiplexer #(.width(8), .enable("false")) multiplexer_2 (
    .in0(DataIn), .in1(multiplexer_1_out), .out(multiplexer_2_out), .sel(shamt[0]));
  _00 u_00_2 (.in_1(multiplexer_2_out), .out_2(n00_2_out_2));
  _01 u_01_2 (.in_1(multiplexer_2_out), .out_2(n01_2_out_2));
  _10 u_10_2 (.in_1(multiplexer_2_out), .out_2(n10_2_out_2));
  _11 u_11_2 (.in_1(multiplexer_2_out), .out_2(n11_2_out_2));
  _00 u_00_3 (.in_1(n00_2_out_2), .out_2(n00_3_out_2));
  _01 u_01_3 (.in_1(n01_2_out_2), .out_2(n01_3_out_2));
  _10 u_10_3 (.in_1(n10_2_out_2), .out_2(n10_3_out_2));
  _11 u_11_3 (.in_1(n11_2_out_2), .out_2(n11_3_out_2));
  Multiplexer #(.select(2), .width(8), .enable("false")) multiplexer_3 (
    .in0(n00_3_out_2), .in1(n01_3_out_2), .in2(n10_3_out_2), .in3(n11_3_out_2), .out(multiplexer_3_out),
    .sel({L_R, A_L}));
  Multiplexer #(.width(8), .enable("false")) multiplexer_4 (
    .in0(multiplexer_2_out), .in1(multiplexer_3_out), .out(multiplexer_4_out), .sel(shamt[1]));
  _00 u_00_4 (.in_1(multiplexer_4_out), .out_2(n00_4_out_2));
  _01 u_01_4 (.in_1(multiplexer_4_out), .out_2(n01_4_out_2));
  _10 u_10_4 (.in_1(multiplexer_4_out), .out_2(n10_4_out_2));
  _11 u_11_4 (.in_1(multiplexer_4_out), .out_2(n11_4_out_2));
  _00 u_00_5 (.in_1(n00_4_out_2), .out_2(n00_5_out_2));
  _00 u_00_6 (.in_1(n00_5_out_2), .out_2(n00_6_out_2));
  _01 u_01_5 (.in_1(n01_6_out_2), .out_2(n01_5_out_2));
  _01 u_01_6 (.in_1(n01_4_out_2), .out_2(n01_6_out_2));
  _10 u_10_5 (.in_1(n10_4_out_2), .out_2(n10_5_out_2));
  _10 u_10_6 (.in_1(n10_5_out_2), .out_2(n10_6_out_2));
  _11 u_11_5 (.in_1(n11_6_out_2), .out_2(n11_5_out_2));
  _11 u_11_6 (.in_1(n11_4_out_2), .out_2(n11_6_out_2));
  _00 u_00_7 (.in_1(n00_6_out_2), .out_2(n00_7_out_2));
  _01 u_01_7 (.in_1(n01_5_out_2), .out_2(n01_7_out_2));
  _10 u_10_7 (.in_1(n10_6_out_2), .out_2(n10_7_out_2));
  _11 u_11_7 (.in_1(n11_5_out_2), .out_2(n11_7_out_2));
  Multiplexer #(.select(2), .width(8), .enable("false")) multiplexer_5 (
    .in0(n00_7_out_2), .in1(n01_7_out_2), .in2(n10_7_out_2), .in3(n11_7_out_2), .out(multiplexer_5_out),
    .sel({L_R, A_L}));
  Multiplexer #(.width(8), .enable("false")) multiplexer_6 (
    .in0(multiplexer_4_out), .in1(multiplexer_5_out), .out(DataOut), .sel(shamt[2]));

  // Other names for the same wires on the sheet: Arth_Logic = A_L; Left_Right = L_R; Din[7:0] = DataIn;
  //   Dout[7:0] = DataOut

  // Notes on the sheet:
  //   L/R,A/L: 00逻辑右移，01算术右移，10逻辑左移，11：循环左移
  //   输入引脚
  //   请勿修改引脚名称、电路名称及电路封装外观
  //   输出引脚
endmodule

module _00 (
  input  [7:0] in_1,
  output [7:0] out_2
);


  assign out_2 = {1'b0, in_1[7:1]};
endmodule

module _01 (
  input  [7:0] in_1,
  output [7:0] out_2
);


  assign out_2 = {{2{in_1[7]}}, in_1[6:1]};
endmodule

module _10 (
  input  [7:0] in_1,
  output [7:0] out_2
);


  assign out_2 = {in_1[6:0], 1'b0};
endmodule

module _11 (
  input  [7:0] in_1,
  output [7:0] out_2
);


  assign out_2 = {in_1[6:0], in_1[7]};
endmodule

module _8_8 (
  input  clk,
  input  [7:0] x,
  input  [7:0] y,
  input  reset,
  output [15:0] out_5
);

  wire main_3_c16, main_6_c16;
  wire [7:0] main_1_prod, main_2_prod, main_4_prod, main_5_prod;
  wire [15:0] bit_extender_1_out, bit_extender_2_out, bit_extender_3_out, bit_extender_4_out, main_3_s,
       main_6_s, shifter_1_out, shifter_2_out, shifter_3_out;

  main main_1 (.CLK(clk), .X(x[3:0]), .Y(y[3:0]), .Prod(main_1_prod), .Reset(reset));
  assign bit_extender_1_out = {{8{1'b0}}, main_1_prod};  // Bit_Extender bit_extender_1
  assign bit_extender_2_out = {{8{1'b0}}, main_2_prod};  // Bit_Extender bit_extender_2
  main main_2 (.CLK(clk), .X(x[7:4]), .Y(y[3:0]), .Prod(main_2_prod), .Reset(reset));
  lab4_2_main main_3 (
    .X(bit_extender_1_out), .Y(shifter_1_out), .C0(1'b0), .S(main_3_s), .C16(main_3_c16));  // open: Pg, Gg
  Shifter #(.width(16)) shifter_1 (.in(bit_extender_2_out), .\dist (4'b0100), .out(shifter_1_out));
  main main_4 (.CLK(clk), .X(x[3:0]), .Y(y[7:4]), .Prod(main_4_prod), .Reset(reset));
  assign bit_extender_3_out = {{8{1'b0}}, main_4_prod};  // Bit_Extender bit_extender_3
  Shifter #(.width(16)) shifter_2 (.in(bit_extender_3_out), .\dist (4'b0100), .out(shifter_2_out));
  main main_5 (.CLK(clk), .X(x[7:4]), .Y(y[7:4]), .Prod(main_5_prod), .Reset(reset));
  lab4_2_main main_6 (
    .X(shifter_2_out), .Y(main_3_s), .C0(main_3_c16), .S(main_6_s), .C16(main_6_c16));  // open: Pg, Gg
  assign bit_extender_4_out = {{8{1'b0}}, main_5_prod};  // Bit_Extender bit_extender_4
  Shifter #(.width(16)) shifter_3 (.in(bit_extender_4_out), .\dist (4'b1000), .out(shifter_3_out));
  lab4_2_main main_7 (.X(main_6_s), .Y(shifter_3_out), .C0(main_6_c16), .S(out_5));  // open: C16, Pg, Gg
endmodule

module _16_16 (
  input  clk,
  input  [15:0] x,
  input  [15:0] y,
  input  reset,
  output [31:0] F
);

  wire adder32_1_cout, adder32_2_cout;
  wire [15:0] n8_8_1_out_5, n8_8_2_out_5, n8_8_3_out_5, n8_8_4_out_5;
  wire [31:0] adder32_1_s, adder32_2_s, bit_extender_1_out, bit_extender_2_out, bit_extender_3_out,
       bit_extender_4_out, shifter_1_out, shifter_2_out, shifter_3_out;

  _8_8 u_8_8_1 (.clk(clk), .x(x[7:0]), .y(y[7:0]), .reset(reset), .out_5(n8_8_1_out_5));
  assign bit_extender_1_out = {{16{1'b0}}, n8_8_1_out_5};  // Bit_Extender bit_extender_1
  _8_8 u_8_8_2 (.clk(clk), .x(x[15:8]), .y(y[7:0]), .reset(reset), .out_5(n8_8_2_out_5));
  Adder32 adder32_1 (
    .Cin(1'b0), .Cout(adder32_1_cout), .X(bit_extender_1_out), .Y(shifter_1_out), .S(adder32_1_s));  // open: OF, CF, ZF, SF
  assign bit_extender_2_out = {{16{1'b0}}, n8_8_2_out_5};  // Bit_Extender bit_extender_2
  _8_8 u_8_8_3 (.clk(clk), .x(x[7:0]), .y(y[15:8]), .reset(reset), .out_5(n8_8_3_out_5));
  Shifter #(.width(32)) shifter_1 (.in(bit_extender_2_out), .\dist (5'b01000), .out(shifter_1_out));
  assign bit_extender_3_out = {{16{1'b0}}, n8_8_3_out_5};  // Bit_Extender bit_extender_3
  _8_8 u_8_8_4 (.clk(clk), .x(x[15:8]), .y(y[15:8]), .reset(reset), .out_5(n8_8_4_out_5));
  Adder32 adder32_2 (
    .Cin(adder32_1_cout), .Cout(adder32_2_cout), .X(adder32_1_s), .Y(shifter_2_out), .S(adder32_2_s));  // open: OF, CF, ZF, SF
  Shifter #(.width(32)) shifter_2 (.in(bit_extender_3_out), .\dist (5'b01000), .out(shifter_2_out));
  assign bit_extender_4_out = {{16{1'b0}}, n8_8_4_out_5};  // Bit_Extender bit_extender_4
  Shifter #(.width(32)) shifter_3 (.in(bit_extender_4_out), .\dist (5'b10000), .out(shifter_3_out));
  Adder32 adder32_3 (.Cin(adder32_2_cout), .X(adder32_2_s), .Y(shifter_3_out), .S(F));  // open: Cout, OF, CF, ZF, SF
endmodule

module _32_32 (
  input  clk,
  input  [31:0] x,
  input  [31:0] y,
  input  reset,
  output [31:0] HIGH32,
  output [31:0] LOW32
);

  wire adder32_1_cout, adder32_2_cout;
  wire [15:0] n16_16_2_f, n16_16_2_f_2, n16_16_3_f, n16_16_3_f_2;
  wire [31:0] adder32_1_s, adder32_3_s, bit_extender_1_out, bit_extender_2_out, bit_extender_3_out,
       bit_extender_4_out, n16_16_1_f, n16_16_4_f, shifter_1_out, shifter_2_out;

  _16_16 u_16_16_1 (.clk(clk), .x(x[15:0]), .y(y[15:0]), .reset(reset), .F(n16_16_1_f));
  _16_16 u_16_16_2 (.clk(clk), .x(x[15:0]), .y(y[31:16]), .reset(reset), .F({n16_16_2_f_2, n16_16_2_f}));
  Adder32 adder32_1 (
    .Cin(1'b0), .Cout(adder32_1_cout), .X(shifter_1_out), .Y(n16_16_1_f), .S(adder32_1_s));  // open: OF, CF, ZF, SF
  assign bit_extender_1_out = {{16{1'b0}}, n16_16_2_f};  // Bit_Extender bit_extender_1
  Shifter #(.width(32)) shifter_1 (.in(bit_extender_1_out), .\dist (5'b10000), .out(shifter_1_out));
  _16_16 u_16_16_3 (.clk(clk), .x(x[31:16]), .y(y[15:0]), .reset(reset), .F({n16_16_3_f_2, n16_16_3_f}));
  assign bit_extender_2_out = {{16{1'b0}}, n16_16_3_f};  // Bit_Extender bit_extender_2
  Shifter #(.width(32)) shifter_2 (.in(bit_extender_2_out), .\dist (5'b10000), .out(shifter_2_out));
  Adder32 adder32_2 (
    .Cin(1'b0), .Cout(adder32_2_cout), .X(shifter_2_out), .Y(adder32_1_s), .S(LOW32));  // open: OF, CF, ZF, SF
  _16_16 u_16_16_4 (.clk(clk), .x(x[31:16]), .y(y[31:16]), .reset(reset), .F(n16_16_4_f));
  assign bit_extender_3_out = {{16{1'b0}}, n16_16_2_f_2};  // Bit_Extender bit_extender_3
  assign bit_extender_4_out = {{16{1'b0}}, n16_16_3_f_2};  // Bit_Extender bit_extender_4
  Adder32 adder32_3 (
    .Cin(adder32_1_cout), .X(bit_extender_4_out), .Y(bit_extender_3_out), .S(adder32_3_s));  // open: Cout, OF, CF, ZF, SF
  Adder32 adder32_4 (.Cin(adder32_2_cout), .X(n16_16_4_f), .Y(adder32_3_s), .S(HIGH32));  // open: Cout, OF, CF, ZF, SF
endmodule
