// Logisim project 思考题2.circ as structural Verilog: 8 circuits, main circuit ALU
module ALU (
  input  [3:0] ALUctr,
  input  [31:0] A,
  input  [31:0] B,
  output Zero,
  output [31:0] S
);

  wire adder32_1_cf, adder32_1_of, adder32_1_sf, aluctrl_1_alctr, aluctrl_1_lrctr, aluctrl_1_sigctr,
       aluctrl_1_subctr, multiplexer_2_out, not_1_out, xor_3_out;
  wire [2:0] aluctrl_1_opctr;
  wire [31:0] adder32_1_s, and_1_out, bit_extender_1_out, bit_extender_2_out, main_1_dataout, or_1_out,
       xor_1_out, xor_2_out;

  assign bit_extender_1_out = {{31{aluctrl_1_subctr}}, aluctrl_1_subctr};  // Bit_Extender bit_extender_1
  assign xor_1_out = bit_extender_1_out ^ B;  // XOR_Gate xor_1, 32 bits wide
  assign and_1_out = A & B;  // AND_Gate and_1, 32 bits wide
  assign or_1_out = A | B;  // OR_Gate or_1, 32 bits wide
  assign xor_2_out = B ^ A;  // XOR_Gate xor_2, 32 bits wide
  lab4_4_main main_1 (
    .L_R(aluctrl_1_lrctr), .shamt(B[4:0]), .DataIn(A), .DataOut(main_1_dataout), .A_L(aluctrl_1_alctr));
  lab4_3_Adder32 adder32_1 (
    .Cin(aluctrl_1_subctr), .X(A), .Y(xor_1_out), .S(adder32_1_s), .OF(adder32_1_of), .CF(adder32_1_cf),
    .ZF(Zero), .SF(adder32_1_sf));  // open: Cout
  xor xor_3 (xor_3_out, adder32_1_of, adder32_1_sf);
  Multiplexer #(.select(3), .width(32), .enable("false")) multiplexer_1 (
    .in0(adder32_1_s), .in1(and_1_out), .in2(or_1_out), .in3(xor_2_out), .in4(main_1_dataout), .in5(B),
    .in6(bit_extender_2_out), .out(S), .sel(aluctrl_1_opctr));  // open: in7
  Multiplexer #(.enable("false")) multiplexer_2 (
    .in0(xor_3_out), .in1(adder32_1_cf), .out(multiplexer_2_out), .sel(not_1_out));
  not not_1 (not_1_out, aluctrl_1_sigctr);
  ALUctrl aluctrl_1 (
    .SUBctr(aluctrl_1_subctr), .LRctr(aluctrl_1_lrctr), .SIGctr(aluctrl_1_sigctr), .ALctr(aluctrl_1_alctr),
    .OPctr(aluctrl_1_opctr), .ALUctr(ALUctr));
  // Probe on A
  // Probe on B
  // Probe on S
  assign bit_extender_2_out = {{31{1'b0}}, multiplexer_2_out};  // Bit_Extender bit_extender_2

  // Other names for the same wires on the sheet: Result[31:0] = S

  // Notes on the sheet:
  //   A: pull=down
  //   B: pull=down
  //   ALUctr: pull=down
  //   新增循环左移功能。由ALUctr=1001控制
  //   输入引脚
  //   请勿修改引脚名称、电路名称及电路封装外观
  //   提示：使用32位并行加法器子电路、桶形移位器、ALU控制子电路实现32位ALU
  //   功能说明:32位ALU，输入32位操作数A、B，4位控制信号ALUctr，输出32位结果Reseult和1位Zero标志位
  //   输出引脚
  //   操作数和结果
endmodule

module ALUctrl (
  input  [3:0] ALUctr,
  output SUBctr,
  output LRctr,
  output SIGctr,
  output ALctr,
  output [2:0] OPctr
);

  wire _0001_out, _0011_out, _0100_out, _0101_out, _0110_out, _0111_out, _1000_out, _1001_out, _1101_out,
       _1111_out;

  and _0001 (_0001_out, ~ALUctr[3], ~ALUctr[2], ~ALUctr[1], ALUctr[0]);  // AND_Gate
  and _0010 (SIGctr, ~ALUctr[3], ~ALUctr[2], ALUctr[1], ~ALUctr[0]);  // AND_Gate
  and _0011 (_0011_out, ~ALUctr[3], ~ALUctr[2], ALUctr[1], ALUctr[0]);  // AND_Gate
  and _0100 (_0100_out, ~ALUctr[3], ALUctr[2], ~ALUctr[1], ~ALUctr[0]);  // AND_Gate
  and _0101 (_0101_out, ~ALUctr[3], ALUctr[2], ~ALUctr[1], ALUctr[0]);  // AND_Gate
  and _0110 (_0110_out, ~ALUctr[3], ALUctr[2], ALUctr[1], ~ALUctr[0]);  // AND_Gate
  and _0111 (_0111_out, ~ALUctr[3], ALUctr[2], ALUctr[1], ALUctr[0]);  // AND_Gate
  and _1000 (_1000_out, ALUctr[3], ~ALUctr[2], ~ALUctr[1], ~ALUctr[0]);  // AND_Gate
  and _1101 (_1101_out, ALUctr[3], ALUctr[2], ~ALUctr[1], ALUctr[0]);  // AND_Gate
  and _1111 (_1111_out, ALUctr[3], ALUctr[2], ALUctr[1], ALUctr[0]);
  and _1001 (_1001_out, ALUctr[3], ~ALUctr[2], ~ALUctr[1], ALUctr[0]);  // AND_Gate
  or or_1 (SUBctr, SIGctr, _0011_out, _1000_out);
  or or_2 (LRctr, _0001_out, _1001_out);
  or or_3 (OPctr[2], _0001_out, SIGctr, _0011_out, _1001_out, _1101_out, _0101_out, _1111_out);
  or or_4 (OPctr[1], SIGctr, _0011_out, _0100_out, _0110_out);
  or or_5 (OPctr[0], _0100_out, _0111_out, _1111_out);
  or or_6 (ALctr, _1101_out, _1001_out);

  // Notes on the sheet:
  //   输入引脚
  //   ALU操作控制信号生成部件
  //   输出引脚
endmodule

module Adder32 (
  input  Cin,
  input  [31:0] X,
  input  [31:0] Y,
  output CF,
  output Cout,
  output OF,
  output SF,
  output [31:0] S,
  output ZF
);

  // Probe on X
  // Probe on Y
  // Probe on S

  // Notes on the sheet:
  //   Y: pull=down
  //   Cin: pull=down
  //   X: pull=down
  //   输入引脚区
  //   输出引脚区
  //   请勿修改引脚名称、电路名称及电路封装外观
  //   提示：使用16位并行加法器子电路实现32位快速加法器
  //   功能说明:32位Adder  S=X+Y，Cout为最高位进位位，Cin为进位输入， S为和，溢出OF、进位CF、零ZF、符号SF。
  //   +
  //   =
  //   无符号加法
endmodule

// 移位器
module Shifter32 (
  input  [4:0] shamt,
  input  L_R,
  input  A_L,
  input  [31:0] DataIn,
  output [31:0] DataOut
);


  // Other names for the same wires on the sheet: Arth_Logic = A_L; Din[31:0] = DataIn; Dout[31:0] = DataOut;
  //   Left_Right = L_R

  // Notes on the sheet:
  //   L/R,A/L: 00逻辑右移，01算术右移，10逻辑左移，11：循环左移
  //   输入引脚
  //   请勿修改引脚名称、电路名称及电路封装外观
  //   提示：使用多路选择器、逻辑门实现32位桶形移位器，禁止直接使用移位器组件。
  //   输出引脚
endmodule

module Adder16 (
  input  C0,
  input  [15:0] X,
  input  [15:0] Y,
  output C16,
  output Pg,
  output Gg,
  output [15:0] S
);

  // Probe on X
  // Probe on Y
  // Probe on S

  // Notes on the sheet:
  //   C0: pull=down
  //   X: pull=down
  //   Y: pull=down
  //   输入引脚区
  //   请勿修改引脚名称、电路名称及电路封装外观
  //   提示：使用4位先行进位加法器和CLU子电路实现16位并行加法器
  //   功能说明:16位Adder  S=X+Y，C16为最高位进位位，C0为进位输入， Pg、Gg为成组进位生成传递函数
  //   输出引脚区
  //   +
  //   =
  //   无符号加法
endmodule

module CLA4 (
  input  [3:0] X,
  input  [3:0] Y,
  input  Cin,
  output [3:0] F,
  output Cout,
  output Pg,
  output Gg
);

  Hex_Digit_Display hex_digit_display_1 (.value(X));  // open: dp
  Hex_Digit_Display hex_digit_display_2 (.value(Y));  // open: dp
  Hex_Digit_Display hex_digit_display_3 (.value(F));  // open: dp

  // Other names for the same wires on the sheet: Z[3:0] = F

  // Notes on the sheet:
  //   +
  //   =
  //   输出
  //   输入
  //   请勿修改引脚名称、电路名称及电路封装外观
  //   提示：使用全加器和CLU子电路实现四位先行进位加法器CLA4
endmodule

module CLU4 (
  input  P0,
  input  P1,
  input  P2,
  input  P3,
  input  G0,
  input  G1,
  input  G2,
  input  G3,
  input  C0,
  output C1,
  output C3,
  output C2,
  output C4,
  output Pg,
  output Gg
);


  // Notes on the sheet:
  //   输入引脚
  //   请勿修改引脚名称、电路名称及电路封装外观
  //   提示：使用逻辑门电路实现4位四位先行进位部件CLU，Pg、Gg为成组进位生成传递函数
  //   输出引脚
endmodule

module FA (
  input  A,
  input  B,
  input  Cin,
  output F,
  output P,
  output G
);


  // Notes on the sheet:
  //   输入引脚
  //   请勿修改引脚名称、电路名称及电路封装外观
  //   全加器
  //   输出引脚
endmodule
