// Logisim project lab5.2.circ as structural Verilog: 2 circuits, main circuit DataRam
// DataRAM
module DataRam (
  input  CLK,
  input  CLR,
  input  WE,
  input  [2:0] MemOp,
  input  [17:0] Addr,
  input  [31:0] Din,
  output AlignErr,
  output [31:0] DataOut
);

  wire sel_1_sel0, sel_1_sel1, sel_1_sel2, sel_1_sel3;
  wire [7:0] multiplexer_1_out_2, multiplexer_2_out;
  wire [15:0] multiplexer_3_out;
  wire [17:0] shifter_1_out;
  wire [23:0] multiplexer_1_out;
  wire [31:0] bit_extender_1_out, bit_extender_2_out, bit_extender_3_out, bit_extender_4_out, ram_1_data;

  Shifter #(.width(18), .shift("lr")) shifter_1 (.in(Addr), .\dist (5'b00010), .out(shifter_1_out));
  Multiplexer #(.select(3), .width(32), .enable("false")) multiplexer_1 (
    .in0(Din), .in1({Din[7:0], Din[7:0], Din[7:0], Din[7:0]}), .in2({Din[15:0], Din[15:0]}),
    .in5({Din[7:0], Din[7:0], Din[7:0], Din[7:0]}), .in6({Din[15:0], Din[15:0]}),
    .out({multiplexer_1_out_2, multiplexer_1_out}), .sel(MemOp));  // open: in3, in4, in7
  sel sel_1 (
    .m2(MemOp[2]), .m1(MemOp[1]), .m0(MemOp[0]), .a1(Addr[1]), .a0(Addr[0]), .SEL3(sel_1_sel3),
    .SEL2(sel_1_sel2), .SEL1(sel_1_sel1), .SEL0(sel_1_sel0), .ERR(AlignErr));
  RAM #(.addrWidth(18), .bus("separate"), .Select("high")) ram_1 (
    .addr(shifter_1_out), .din(multiplexer_1_out[7:0]), .data(ram_1_data[7:0]), .str(WE), .sel(sel_1_sel0),
    .clk(CLK), .clr(CLR));  // open: ld
  RAM #(.addrWidth(18), .bus("separate"), .Select("high")) ram_2 (
    .addr(shifter_1_out), .din(multiplexer_1_out[15:8]), .data(ram_1_data[15:8]), .str(WE), .sel(sel_1_sel1),
    .clk(CLK), .clr(CLR));  // open: ld
  Multiplexer #(.select(2), .width(8), .enable("false")) multiplexer_2 (
    .in0(ram_1_data[7:0]), .in1(ram_1_data[15:8]), .in2(ram_1_data[23:16]), .in3(ram_1_data[31:24]),
    .out(multiplexer_2_out), .sel(Addr[1:0]));
  RAM #(.addrWidth(18), .bus("separate"), .Select("high")) ram_3 (
    .addr(shifter_1_out), .din(multiplexer_1_out[23:16]), .data(ram_1_data[23:16]), .str(WE),
    .sel(sel_1_sel2), .clk(CLK), .clr(CLR));  // open: ld
  assign bit_extender_1_out = {{24{1'b0}}, multiplexer_2_out};  // Bit_Extender bit_extender_1
  assign bit_extender_2_out = {{24{multiplexer_2_out[7]}}, multiplexer_2_out};  // Bit_Extender bit_extender_2
  Multiplexer #(.select(2), .width(16), .enable("false")) multiplexer_3 (
    .in0(ram_1_data[15:0]), .in2(ram_1_data[31:16]), .out(multiplexer_3_out), .sel(Addr[1:0]));  // open: in1, in3
  RAM #(.addrWidth(18), .bus("separate"), .Select("high")) ram_4 (
    .addr(shifter_1_out), .din(multiplexer_1_out_2), .data(ram_1_data[31:24]), .str(WE), .sel(sel_1_sel3),
    .clk(CLK), .clr(CLR));  // open: ld
  assign bit_extender_3_out = {{16{1'b0}}, multiplexer_3_out};  // Bit_Extender bit_extender_3
  assign bit_extender_4_out = {{16{multiplexer_3_out[15]}}, multiplexer_3_out};  // Bit_Extender bit_extender_4
  Multiplexer #(.select(3), .width(32), .enable("false")) multiplexer_4 (
    .in0(ram_1_data), .in1(bit_extender_1_out), .in2(bit_extender_3_out), .in5(bit_extender_2_out),
    .in6(bit_extender_4_out), .out(DataOut), .sel(MemOp));  // open: in3, in4, in7

  // Other names for the same wires on the sheet: addr_t[1:0] = Addr[1:0]; Dout[31:0] = DataOut

  // Notes on the sheet:
  //   输入引脚
  //   请勿修改引脚名称、电路名称及电路封装外观
  //   为了后续实验中的引用，不要修改MemOp的编码定义、引脚名称和在布局中的位置。
  //   32位数据存储器，按字节分4片存储，可按照字节、半字和字进行存储；读取字节或半字时，支持0扩展和符号位扩展。
  //   输出引脚
endmodule

module sel (
  input  m2,
  input  m1,
  input  m0,
  input  a1,
  input  a0,
  output SEL3,
  output SEL2,
  output SEL1,
  output SEL0,
  output ERR
);

  wire and_1_out, and_2_out, and_3_out, and_4_out, and_5_out, and_6_out, and_7_out, and_8_out, and_9_out;

  and and_1 (and_1_out, ~m2, ~m1, ~m0, ~a1, ~a0);  // AND_Gate
  and and_2 (and_2_out, ~m1, m0, a1, a0);  // AND_Gate
  and and_3 (and_3_out, m1, ~m0, a1, ~a0);  // AND_Gate
  and and_4 (and_4_out, ~m1, m0, a1, ~a0);  // AND_Gate
  and and_5 (and_5_out, ~m1, m0, ~a1, a0);  // AND_Gate
  and and_6 (and_6_out, m1, ~m0, ~a1, ~a0);  // AND_Gate
  and and_7 (and_7_out, ~m1, m0, ~a1, ~a0);  // AND_Gate
  and and_8 (and_8_out, ~m1, m0);  // AND_Gate
  and and_9 (and_9_out, m1, ~m0, ~a0);  // AND_Gate
  or or_1 (SEL3, and_1_out, and_2_out, and_3_out);
  or or_2 (SEL2, and_1_out, and_4_out, and_3_out);
  or or_3 (SEL1, and_1_out, and_5_out, and_6_out);
  or or_4 (SEL0, and_1_out, and_7_out, and_6_out);
  nor nor_1 (ERR, and_1_out, and_8_out, and_9_out);
endmodule
