// Logisim project lab6.1.circ as structural Verilog: 9 circuits, main circuit 控制器
module \控制器  (
  input  [6:0] opcode,
  input  [2:0] funct3,
  input  [6:0] funct7,
  output [2:0] ExtOp,
  output RegWr,
  output [2:0] BandJ,
  output ALUASrc,
  output [1:0] ALUBSrc,
  output [3:0] ALUctr,
  output MemtoReg,
  output [2:0] MemOp,
  output MemWr,
  output halt
);

  wire and_1_out, and_2_out, comparator_1_eq, comparator_2_eq, comparator_3_eq, comparator_4_eq,
       comparator_5_eq, comparator_6_eq, or_1_out;

  extop extop_1 (.opcode(opcode), .out_2(ExtOp[2]), .out_3(ExtOp[1]), .out_4(ExtOp[0]));
  Comparator #(.width(7), .mode("unsigned")) comparator_1 (
    .a(opcode), .b(7'b0110111), .eq(comparator_1_eq));  // open: gt, lt
  Comparator #(.width(7), .mode("unsigned")) comparator_2 (
    .a(opcode), .b(7'b0010111), .eq(comparator_2_eq));  // open: gt, lt
  Comparator #(.width(7), .mode("unsigned")) comparator_3 (
    .a(opcode), .b(7'b1101111), .eq(comparator_3_eq));  // open: gt, lt
  Comparator #(.width(7), .mode("unsigned")) comparator_4 (
    .a(opcode), .b(7'b1100111), .eq(comparator_4_eq));  // open: gt, lt
  Comparator #(.width(7), .mode("unsigned")) comparator_5 (
    .a(opcode), .b(7'b0010011), .eq(comparator_5_eq));  // open: gt, lt
  Comparator #(.width(7), .mode("unsigned")) comparator_6 (
    .a(opcode), .b(7'b0110011), .eq(comparator_6_eq));  // open: gt, lt
  Comparator #(.width(7), .mode("unsigned")) comparator_7 (.a(opcode), .b(7'b1100011), .eq(BandJ[2]));  // open: gt, lt
  Comparator #(.width(7), .mode("unsigned")) comparator_8 (.a(opcode), .b(7'b0000011), .eq(MemtoReg));  // open: gt, lt
  Comparator #(.width(7), .mode("unsigned")) comparator_9 (.a(opcode), .b(7'b0100011), .eq(MemWr));  // open: gt, lt
  Comparator #(.width(7), .mode("unsigned")) comparator_10 (.a(opcode), .b(7'b1110011), .eq(halt));  // open: gt, lt
  or or_1 (or_1_out, comparator_1_eq, comparator_2_eq);
  or or_2 (ALUBSrc[0], comparator_3_eq, comparator_4_eq);
  and and_1 (and_1_out, BandJ[2], funct3[2]);
  and and_2 (and_2_out, BandJ[2], funct3[0]);
  or or_3 (RegWr, or_1_out, ALUBSrc[0], comparator_5_eq, comparator_6_eq, MemtoReg);
  or or_4 (ALUASrc, comparator_2_eq, ALUBSrc[0]);
  or or_5 (ALUBSrc[1], or_1_out, comparator_5_eq, MemtoReg, MemWr);
  or or_6 (BandJ[1], and_1_out, comparator_4_eq);
  or or_7 (BandJ[0], and_2_out, comparator_3_eq);
  mem0 mem0_1 (.opcode(opcode), .funct3(funct3), .out_3(MemOp[0]));
  mem1 mem1_1 (.opcode(opcode), .funct3(funct3), .out_3(MemOp[1]));
  mem2 mem2_1 (.opcode(opcode), .funct3(funct3), .out_3(MemOp[2]));
  alu0 alu0_1 (.opcode(opcode), .funct3(funct3), .in_3(funct7[5]), .out_4(ALUctr[0]));
  alu1 alu1_1 (.opcode(opcode), .funct3(funct3), .in_3(funct7[5]), .out_4(ALUctr[1]));
  alu2 alu2_1 (.opcode(opcode), .funct3(funct3), .in_3(funct7[5]), .out_4(ALUctr[2]));
  alu3 alu3_1 (.opcode(opcode), .funct3(funct3), .in_3(funct7[5]), .out_4(ALUctr[3]));

  // Notes on the sheet:
  //   输入引脚
  //   请勿修改引脚名称、电路名称及电路封装外观
  //   提示：根据指令种类，把7位指令code用一位指令类型标志位来表示，再通过功能码来区分具体指令，生成控制信号。
  //   输出引脚
endmodule

module mem0 (
  input  [6:0] opcode,
  input  [2:0] funct3,
  output out_3
);

  wire and_1_out, and_2_out, or_1_out;

  and and_1 (and_1_out, ~opcode[6], ~opcode[4], ~opcode[3], ~opcode[2], opcode[1], opcode[0], ~funct3[1], ~funct3[0]);  // AND_Gate
  and and_2 (and_2_out, opcode[5], ~funct3[2]);  // AND_Gate
  or or_1 (or_1_out, ~opcode[5], and_2_out);  // OR_Gate
  and and_3 (out_3, and_1_out, or_1_out);
endmodule

module mem1 (
  input  [6:0] opcode,
  input  [2:0] funct3,
  output out_3
);

  wire and_1_out, and_2_out, or_1_out;

  and and_1 (and_1_out, ~opcode[6], ~opcode[4], ~opcode[3], ~opcode[2], opcode[1], opcode[0], ~funct3[1], funct3[0]);  // AND_Gate
  and and_2 (and_2_out, ~opcode[5], funct3[2]);  // AND_Gate
  or or_1 (or_1_out, and_2_out, ~funct3[2]);  // OR_Gate
  and and_3 (out_3, and_1_out, or_1_out);
endmodule

module mem2 (
  input  [6:0] opcode,
  input  [2:0] funct3,
  output out_3
);

  and and_1 (out_3, ~opcode[6], ~opcode[4], ~opcode[3], ~opcode[2], opcode[1], opcode[0], ~funct3[2], ~funct3[1]);  // AND_Gate
endmodule

module alu0 (
  input  [6:0] opcode,
  input  [2:0] funct3,
  input  in_3,
  output out_4
);

  wire and_1_out, and_2_out, and_3_out, and_4_out, and_5_out, and_6_out, and_7_out, and_8_out, and_9_out,
       and_10_out, and_11_out, and_12_out, and_13_out, and_14_out, and_15_out, nand_1_out, or_1_out, or_2_out;

  and and_1 (and_1_out, ~opcode[3], opcode[1], opcode[0]);  // AND_Gate
  and and_2 (and_2_out, funct3[1], funct3[0]);
  and and_3 (and_3_out, ~opcode[6], opcode[5], opcode[4], opcode[2]);  // AND_Gate
  and and_4 (and_4_out, ~opcode[6], ~opcode[5], opcode[4], ~opcode[2]);  // AND_Gate
  and and_5 (and_5_out, ~opcode[6], opcode[5], opcode[4], ~opcode[2]);  // AND_Gate
  and and_6 (and_6_out, opcode[6], opcode[5], ~opcode[4], ~opcode[2]);  // AND_Gate
  and and_7 (and_7_out, ~funct3[1], funct3[0], ~in_3);  // AND_Gate
  and and_8 (and_8_out, funct3[2], ~funct3[1], funct3[0], in_3);  // AND_Gate
  nand nand_1 (nand_1_out, funct3[2], funct3[1]);
  and and_9 (and_9_out, nand_1_out, funct3[0], ~in_3);  // AND_Gate
  and and_10 (and_10_out, funct3[2], funct3[1]);
  and and_11 (and_11_out, and_10_out, funct3[0], ~in_3);  // AND_Gate
  or or_1 (or_1_out, and_2_out, and_7_out, and_8_out);
  or or_2 (or_2_out, and_8_out, and_9_out, and_11_out);
  and and_12 (and_12_out, and_1_out, and_3_out);
  and and_13 (and_13_out, and_1_out, and_4_out, or_1_out);
  and and_14 (and_14_out, and_1_out, and_5_out, or_2_out);
  and and_15 (and_15_out, and_1_out, and_6_out, and_10_out);
  or or_3 (out_4, and_12_out, and_13_out, and_14_out, and_15_out);
endmodule

module alu1 (
  input  [6:0] opcode,
  input  [2:0] funct3,
  input  in_3,
  output out_4
);

  wire and_1_out, and_2_out, and_3_out, and_4_out, and_5_out, and_6_out, and_7_out, and_8_out, and_9_out,
       and_10_out, and_11_out, or_1_out, or_2_out;

  and and_1 (and_1_out, ~opcode[3], opcode[1], opcode[0]);  // AND_Gate
  and and_2 (and_2_out, ~opcode[6], opcode[5], opcode[4], opcode[2]);  // AND_Gate
  and and_3 (and_3_out, ~opcode[6], ~opcode[5], opcode[4], ~opcode[2]);  // AND_Gate
  and and_4 (and_4_out, ~opcode[6], opcode[5], opcode[4], ~opcode[2]);  // AND_Gate
  and and_5 (and_5_out, opcode[6], opcode[5], ~opcode[4], ~opcode[2]);  // AND_Gate
  and and_6 (and_6_out, ~funct3[2], funct3[1], ~in_3);  // AND_Gate
  and and_7 (and_7_out, funct3[2], funct3[1], ~in_3);  // AND_Gate
  or or_1 (or_1_out, funct3[2], ~funct3[1]);  // OR_Gate
  or or_2 (or_2_out, and_6_out, and_7_out);
  and and_8 (and_8_out, and_1_out, and_2_out);
  and and_9 (and_9_out, and_1_out, and_3_out, funct3[1]);
  and and_10 (and_10_out, and_1_out, or_2_out, and_4_out);
  and and_11 (and_11_out, and_1_out, and_5_out, or_1_out);
  or or_3 (out_4, and_8_out, and_9_out, and_10_out, and_11_out);
endmodule

module alu2 (
  input  [6:0] opcode,
  input  [2:0] funct3,
  input  in_3,
  output out_4
);

  wire and_1_out, and_2_out, and_3_out, and_4_out, and_5_out, and_6_out, and_7_out, and_8_out, and_9_out,
       and_10_out, and_11_out, and_12_out, or_1_out, or_2_out;

  and and_1 (and_1_out, funct3[2], ~and_2_out);  // AND_Gate
  and and_2 (and_2_out, ~funct3[1], funct3[0]);  // AND_Gate
  and and_3 (and_3_out, funct3[2], ~funct3[1], funct3[0]);  // AND_Gate
  and and_4 (and_4_out, funct3[2], ~in_3);  // AND_Gate
  and and_5 (and_5_out, ~opcode[6], opcode[4], opcode[1], opcode[0]);  // AND_Gate
  and and_6 (and_6_out, opcode[5], ~opcode[3], opcode[2]);  // AND_Gate
  and and_7 (and_7_out, ~opcode[5], ~opcode[3], ~opcode[2]);  // AND_Gate
  and and_8 (and_8_out, opcode[5], ~opcode[3], ~opcode[2]);  // AND_Gate
  or or_1 (or_1_out, and_1_out, and_3_out);
  and and_9 (and_9_out, and_3_out, in_3);
  or or_2 (or_2_out, and_4_out, and_9_out);
  and and_10 (and_10_out, and_5_out, and_6_out);
  and and_11 (and_11_out, and_5_out, and_7_out, or_1_out);
  and and_12 (and_12_out, and_5_out, and_8_out, or_2_out);
  or or_3 (out_4, and_10_out, and_11_out, and_12_out);
endmodule

module alu3 (
  input  [6:0] opcode,
  input  [2:0] funct3,
  input  in_3,
  output out_4
);

  wire and_1_out, and_2_out, and_3_out, and_4_out, and_5_out, and_6_out, and_7_out, and_8_out, and_9_out,
       or_1_out;

  and and_1 (and_1_out, ~opcode[6], opcode[4], ~opcode[3], opcode[1], opcode[0]);  // AND_Gate
  and and_2 (and_2_out, opcode[5], opcode[2]);
  and and_3 (and_3_out, ~opcode[5], ~opcode[2]);  // AND_Gate
  and and_4 (and_4_out, opcode[5], ~opcode[2]);  // AND_Gate
  and and_5 (and_5_out, funct3[2], ~funct3[1], funct3[0]);  // AND_Gate
  or or_1 (or_1_out, and_5_out, and_6_out);
  and and_6 (and_6_out, ~funct3[2], ~funct3[1], ~funct3[0]);  // AND_Gate
  and and_7 (and_7_out, and_1_out, and_2_out);
  and and_8 (and_8_out, and_1_out, and_3_out, and_5_out, in_3);
  and and_9 (and_9_out, and_1_out, and_4_out, or_1_out, in_3);
  or or_2 (out_4, and_7_out, and_8_out, and_9_out);
endmodule

module extop (
  input  [6:0] opcode,
  output out_2,
  output out_3,
  output out_4
);

  wire and_3_out, and_4_out, or_1_out;

  and and_1 (out_2, opcode[6], opcode[5], opcode[3], opcode[2], opcode[1], opcode[0]);
  and and_2 (out_3, opcode[5], ~opcode[4], ~opcode[3], ~opcode[2], opcode[1], opcode[0]);  // AND_Gate
  and and_3 (and_3_out, ~opcode[6], opcode[4], opcode[2]);  // AND_Gate
  and and_4 (and_4_out, opcode[6], opcode[5], ~opcode[4], ~opcode[2]);  // AND_Gate
  or or_1 (or_1_out, and_3_out, and_4_out);
  and and_5 (out_4, or_1_out, ~opcode[3], opcode[1], opcode[0]);  // AND_Gate
endmodule
